// Logisim project TinyCPU.circ as structural Verilog: 6 circuits, main circuit TinyCPU
module TinyCPU (
  input  CLK,
  output HALTED
);

  wire errorflags_1_ovf_out, fetchdecode_1_load_const, memory_1_valid_out;
  wire [15:0] addresspath_1_address, datapath_1_acc_out;

  FetchDecode fetchdecode_1 (
    .DEC_JUMP_NOT_ZERO(CLK), .LOAD_CONST(fetchdecode_1_load_const));  // open: NOT_ZERO, CLK, RESET, PROGRAM_LIMIT, DEC_HALT_ERROR, ZERO, NEGATIVE, ERROR, OPERAND, OPCODE, LOAD_ADDRESS, LOAD_ADDRESS_REGISTER, LOAD_ADDRESS_REGISTER_PLUS_OFFSET, ADD_CONST, ADD_ADDRESS, ADD_ADDRESS_REGISTER, JUMP_NOT_ZERO, ADD_ADDRESS_REGISTER_PLUS_OFFSET, SUB_CONST, SUB_ADDRESS, SUB_ADDRESS_REGISTER, HALT_ERROR, SUB_ADDRESS_REGISTER_PLUS_OFFSET, MUL_CONST, MUL_ADDRESS, MUL_ADDRESS_REGISTER, MUL_ADDRESS_REGISTER_PLUS_OFFSET, DIV_CONST, PC_OUT, DIV_ADDRESS, DIV_ADDRESS_REGISTER, DIV_ADDRESS_REGISTER_PLUS_OFFSET, AND_CONST, AND_ADDRESS, AND_ADDRESS_REGISTER, AND_ADDRESS_REGISTER_PLUS_OFFSET, OPCODE_2, OR_CONST, OR_ADDRESS, OR_ADDRESS_REGISTER, OR_ADDRESS_REGISTER_PLUS_OFFSET, STORE_ADDRESS, STORE_ADDRESS_REGISTER, STORE_ADDRESS_REGISTER_PLUS_OFFSET, LOAD_ADDRESS_REGISTER_CONST, LOAD_ADDRESS_REGISTER_ADDRESS, NOT, JUMP_ADDRESS, JUMP_ZERO, JUMP_NEGATIVE, JUMP_ERROR, JUMP_NOT_ERROR, CLEAR_ERROR, INPUT, PRINT, PRINT_ADDRESS, HALT, SET_OVF, SET_DIV0, SET_ADDR, SET_INV, SET_ILL, SET_INPUT
  Datapath datapath_1 (.ACC_OUT(datapath_1_acc_out));  // open: DATA_IN, ACC_LOAD, VALID_IN, CLK, ZERO, NEGATIVE, ACC_VALID_OUT
  AddressPath addresspath_1 (.ADDRESS(addresspath_1_address));  // open: ADDRESS_IN, AR_LOAD, OFFSET, VALID_IN, CLK, ADDRESS_PLUS_OFFSET, OFFSET_CARRY, ADDRESS_VALID
  Memory memory_1 (.VALID_OUT(memory_1_valid_out));  // open: ADDRESS, WRITE_ENABLE, CLK, VALID_IN, DATA_IN, DATA_OUT
  ErrorFlags errorflags_1 (.OVF_OUT(errorflags_1_ovf_out));  // open: CLEAR_ERROR, CLK, SET_OVF, SET_DIV0, SET_ADDR, SET_INV, SET_ILL, SET_INPUT, DIV0_OUT, ADDR_OUT, INV_OUT, ILL_OUT, INPUT_OUT

  // Notes on the sheet:
  //   TinyCPU AP 5: countdown fixture and clock-edge trace boundary
endmodule

module Datapath (
  input  [15:0] DATA_IN,
  input  ACC_LOAD,
  input  VALID_IN,
  input  CLK,
  output [15:0] ACC_OUT,
  output ZERO,
  output NEGATIVE,
  output ACC_VALID_OUT
);

  Register #(.width(16)) ACC (.D(DATA_IN), .en(ACC_LOAD), .clk(CLK), .Q(ACC_OUT));  // open: clr
  Register #(.width(1)) ACC_VALID (.D(VALID_IN), .en(CLK), .clk(ACC_LOAD), .Q(ACC_VALID_OUT));  // open: clr
  Comparator #(.width(16)) ACC_STATUS (.a(ACC_OUT), .b({16{1'b0}}), .eq(ZERO), .lt(NEGATIVE));  // open: gt

  // Notes on the sheet:
  //   Clocked 16-bit accumulator; signed comparator derives ZERO and NEGATIVE
endmodule

module AddressPath (
  input  [15:0] ADDRESS_IN,
  input  AR_LOAD,
  input  [15:0] OFFSET,
  input  VALID_IN,
  input  CLK,
  output [15:0] ADDRESS,
  output [15:0] ADDRESS_PLUS_OFFSET,
  output OFFSET_CARRY,
  output ADDRESS_VALID
);

  Register #(.width(16)) AR (.D(ADDRESS_IN), .en(AR_LOAD), .clk(CLK), .Q(ADDRESS));  // open: clr
  Register #(.width(1)) AR_VALID (.D(VALID_IN), .en(AR_LOAD), .clk(CLK), .Q(ADDRESS_VALID));  // open: clr
  Adder #(.width(16)) OFFSET_ADDER (
    .a(ADDRESS), .b(OFFSET), .out(ADDRESS_PLUS_OFFSET), .cout(OFFSET_CARRY));  // open: cin

  // Notes on the sheet:
  //   Clocked 12-bit address register with combinational offset addition
endmodule

module Memory (
  input  [15:0] ADDRESS,
  input  WRITE_ENABLE,
  input  CLK,
  input  VALID_IN,
  input  [15:0] DATA_IN,
  output VALID_OUT,
  output [15:0] DATA_OUT
);

  RAM #(.addrWidth(12), .dataWidth(1)) VALID_RAM (
    .addr(ADDRESS[11:0]), .we(WRITE_ENABLE), .oe(1'b1), .clk(CLK), .din(VALID_IN), .dout(VALID_OUT));
  RAM #(.addrWidth(12), .dataWidth(16)) DATA_RAM (
    .addr(ADDRESS[11:0]), .we(WRITE_ENABLE), .oe(1'b1), .clk(CLK), .din(DATA_IN), .dout(DATA_OUT));

  // Notes on the sheet:
  //   4096-word value/valid memory with shared address, write-enable, and clock
endmodule

module ErrorFlags (
  input  CLEAR_ERROR,
  input  CLK,
  input  SET_OVF,
  input  SET_DIV0,
  input  SET_ADDR,
  input  SET_INV,
  input  SET_ILL,
  input  SET_INPUT,
  output OVF_OUT,
  output DIV0_OUT,
  output ADDR_OUT,
  output INV_OUT,
  output ILL_OUT,
  output INPUT_OUT
);

  wire HOLD_ADDR_out, HOLD_DIV0_out, HOLD_ILL_out, HOLD_INPUT_out, HOLD_INV_out, HOLD_OVF_out, NEXT_ADDR_out,
       NEXT_DIV0_out, NEXT_ILL_out, NEXT_INPUT_out, NEXT_INV_out, NEXT_OVF_out, NOT_CLEAR_ERROR_out;

  not NOT_CLEAR_ERROR (NOT_CLEAR_ERROR_out, CLEAR_ERROR);
  and HOLD_OVF (HOLD_OVF_out, OVF_OUT, NOT_CLEAR_ERROR_out);
  and HOLD_DIV0 (HOLD_DIV0_out, DIV0_OUT, NOT_CLEAR_ERROR_out);
  and HOLD_ADDR (HOLD_ADDR_out, ADDR_OUT, NOT_CLEAR_ERROR_out);
  and HOLD_INV (HOLD_INV_out, INV_OUT, NOT_CLEAR_ERROR_out);
  and HOLD_ILL (HOLD_ILL_out, ILL_OUT, NOT_CLEAR_ERROR_out);
  and HOLD_INPUT (HOLD_INPUT_out, INPUT_OUT, NOT_CLEAR_ERROR_out);
  or NEXT_OVF (NEXT_OVF_out, SET_OVF, HOLD_OVF_out);
  or NEXT_DIV0 (NEXT_DIV0_out, SET_DIV0, HOLD_DIV0_out);
  or NEXT_ADDR (NEXT_ADDR_out, SET_ADDR, HOLD_ADDR_out);
  or NEXT_INV (NEXT_INV_out, SET_INV, HOLD_INV_out);
  or NEXT_ILL (NEXT_ILL_out, SET_ILL, HOLD_ILL_out);
  or NEXT_INPUT (NEXT_INPUT_out, SET_INPUT, HOLD_INPUT_out);
  Register #(.width(1)) OVF (.D(NEXT_OVF_out), .en(1'b1), .clk(CLK), .Q(OVF_OUT));  // open: clr
  Register #(.width(1)) DIV0 (.D(NEXT_DIV0_out), .en(1'b1), .clk(CLK), .Q(DIV0_OUT));  // open: clr
  Register #(.width(1)) ADDR (.D(NEXT_ADDR_out), .en(1'b1), .clk(CLK), .Q(ADDR_OUT));  // open: clr
  Register #(.width(1)) INV (.D(NEXT_INV_out), .en(1'b1), .clk(CLK), .Q(INV_OUT));  // open: clr
  Register #(.width(1)) ILL (.D(NEXT_ILL_out), .en(1'b1), .clk(CLK), .Q(ILL_OUT));  // open: clr
  Register #(.width(1)) INPUT (.D(NEXT_INPUT_out), .en(1'b1), .clk(CLK), .Q(INPUT_OUT));  // open: clr

  // Other names for the same wires on the sheet: CURRENT_ADDR = ADDR_OUT; CURRENT_DIV0 = DIV0_OUT;
  //   CURRENT_ILL = ILL_OUT; CURRENT_INPUT = INPUT_OUT; CURRENT_INV = INV_OUT; CURRENT_OVF = OVF_OUT

  // Notes on the sheet:
  //   Set-dominant sticky flags: SET OR (current AND NOT CLEAR_ERROR)
endmodule

module FetchDecode (
  input  DEC_JUMP_NOT_ZERO,
  input  NOT_ZERO,
  input  CLK,
  input  RESET,
  input  [15:0] PROGRAM_LIMIT,
  input  DEC_HALT_ERROR,
  input  ZERO,
  input  NEGATIVE,
  input  ERROR,
  input  [15:0] OPERAND,
  input  [5:0] OPCODE,
  output LOAD_CONST,
  output LOAD_ADDRESS,
  output LOAD_ADDRESS_REGISTER,
  output LOAD_ADDRESS_REGISTER_PLUS_OFFSET,
  output ADD_CONST,
  output ADD_ADDRESS,
  output ADD_ADDRESS_REGISTER,
  output JUMP_NOT_ZERO,
  output ADD_ADDRESS_REGISTER_PLUS_OFFSET,
  output SUB_CONST,
  output SUB_ADDRESS,
  output SUB_ADDRESS_REGISTER,
  output HALT_ERROR,
  output SUB_ADDRESS_REGISTER_PLUS_OFFSET,
  output MUL_CONST,
  output MUL_ADDRESS,
  output MUL_ADDRESS_REGISTER,
  output MUL_ADDRESS_REGISTER_PLUS_OFFSET,
  output DIV_CONST,
  output [15:0] PC_OUT,
  output DIV_ADDRESS,
  output DIV_ADDRESS_REGISTER,
  output DIV_ADDRESS_REGISTER_PLUS_OFFSET,
  output AND_CONST,
  output AND_ADDRESS,
  output AND_ADDRESS_REGISTER,
  output AND_ADDRESS_REGISTER_PLUS_OFFSET,
  output [21:0] OPCODE_2,
  output OR_CONST,
  output OR_ADDRESS,
  output OR_ADDRESS_REGISTER,
  output OR_ADDRESS_REGISTER_PLUS_OFFSET,
  output STORE_ADDRESS,
  output STORE_ADDRESS_REGISTER,
  output STORE_ADDRESS_REGISTER_PLUS_OFFSET,
  output LOAD_ADDRESS_REGISTER_CONST,
  output LOAD_ADDRESS_REGISTER_ADDRESS,
  output NOT,
  output JUMP_ADDRESS,
  output JUMP_ZERO,
  output JUMP_NEGATIVE,
  output JUMP_ERROR,
  output JUMP_NOT_ERROR,
  output CLEAR_ERROR,
  output INPUT,
  output PRINT,
  output PRINT_ADDRESS,
  output HALT,
  output SET_OVF,
  output SET_DIV0,
  output SET_ADDR,
  output SET_INV,
  output SET_ILL,
  output SET_INPUT
);

  wire PC_RANGE_eq, PC_SOURCE_p1;
  wire [15:0] PC_INCREMENT_out;
  wire [15:12] PC_q;

  Register #(.width(16)) PC (.D(PC_INCREMENT_out), .clk(CLK), .Q({PC_q, PC_OUT[11:1], NOT}), .clr(RESET));  // open: en
  Comparator #(.width(16)) PC_RANGE (
    .a(PROGRAM_LIMIT), .b({PC_q, PC_OUT[11:1], NOT}), .eq(PC_RANGE_eq));  // open: gt, lt
  Adder #(.width(16)) PC_INCREMENT (
    .a({PC_q, PC_OUT[11:1], NOT}), .b({16{1'b1}}), .out(PC_INCREMENT_out));  // open: cin, cout
  ROM #(.addrWidth(12), .dataWidth(22)) INSTRUCTION_ROM (.addr({PC_OUT[11:1], NOT}), .data(OPCODE_2));
  Decoder #(.select(6)) ISA_DECODER (
    .out0(LOAD_ADDRESS), .out1(LOAD_ADDRESS_REGISTER), .out2(LOAD_ADDRESS_REGISTER_PLUS_OFFSET),
    .out3(ADD_CONST), .out4(ADD_ADDRESS_REGISTER), .out5(ADD_ADDRESS_REGISTER_PLUS_OFFSET), .out6(SUB_CONST),
    .out7(SUB_ADDRESS), .out8(SUB_ADDRESS_REGISTER), .out9(SUB_ADDRESS_REGISTER_PLUS_OFFSET),
    .out10(MUL_CONST), .out11(MUL_ADDRESS), .out12(MUL_ADDRESS_REGISTER),
    .out13(MUL_ADDRESS_REGISTER_PLUS_OFFSET), .out14(DIV_CONST), .out15(DIV_ADDRESS),
    .out16(DIV_ADDRESS_REGISTER), .out17(DIV_ADDRESS_REGISTER_PLUS_OFFSET), .out18(AND_CONST),
    .out19(AND_ADDRESS), .out20(AND_ADDRESS_REGISTER), .out21(AND_ADDRESS_REGISTER_PLUS_OFFSET),
    .out22(OR_CONST), .out23(OR_ADDRESS), .out24(OR_ADDRESS_REGISTER),
    .out25(OR_ADDRESS_REGISTER_PLUS_OFFSET), .out26(STORE_ADDRESS_REGISTER),
    .out27(STORE_ADDRESS_REGISTER_PLUS_OFFSET), .out28(LOAD_ADDRESS_REGISTER_CONST),
    .out29(LOAD_ADDRESS_REGISTER_ADDRESS), .out30(NOT), .out31(JUMP_ADDRESS), .out32(JUMP_ZERO),
    .out33(JUMP_NEGATIVE), .out34(JUMP_ERROR), .out35(JUMP_NOT_ERROR), .out36(CLEAR_ERROR), .out37(INPUT),
    .out38(PRINT_ADDRESS), .out39(SET_OVF), .out40(SET_DIV0), .out41(SET_INV), .out42(SET_ILL),
    .out43(SET_INPUT), .sel(OPCODE));  // open: out44, out45, out46, out47, out48, out49, out50, out51, out52, out53, out54, out55, out56, out57, out58, out59, out60, out61, out62, out63, en
  // Multiplexer #(.width(16)) PC_SOURCE: pin names not known; wires that end beside it: PC_SOURCE_p1
  // AND_Gate JNZ_TAKEN: pin names not known; wires that end beside it: DEC_JUMP_NOT_ZERO, NOT_ZERO, JUMP_NOT_ZERO
  or ERROR_HALT (AND_CONST, PC_RANGE_eq, DEC_HALT_ERROR);
  // Pins of 1 and 12 and 16 bits meet at {PC_OUT[15:1], NOT}

  assign HALT_ERROR = AND_CONST;
  assign PC_OUT[0] = NOT;

  // Notes on the sheet:
  //   PROGRAM_LIMIT: initial=0xfff
  //   AP 7 machine format v1: stable six-bit opcode allocation and encoder-generated ROM
  //   contents of INSTRUCTION_ROM (hex, n*v repeats v):
  //   3fffff 65 3 64 0 65 64 4
endmodule
