// Logisim project TinyCPU-AddSub.circ as structural Verilog: 1 circuit, main circuit AddSub
module AddSub (
  input  [31:0] OPERANDS,
  input  [1:0] VALID,
  input  SUBTRACT,
  output CARRY,
  output [15:0] RESULT,
  output RESULT_VALID
);

  wire BOTH_VALID_out, undriven, undriven_2;
  wire [15:0] ADD_out, SUB_out, undriven_3, undriven_4;

  Adder #(.width(16)) ADD (.a(undriven_3), .b(undriven_4), .out(ADD_out), .cin(1'b1), .cout(CARRY));
  Subtractor #(.width(16)) SUB (.a(undriven_3), .b(undriven_4), .out(SUB_out));  // open: bin, bout
  and BOTH_VALID (BOTH_VALID_out, undriven, undriven_2);
  Multiplexer #(.width(16)) ADD_SUB_SELECT (.in0(ADD_out), .in1(SUB_out), .out(RESULT), .sel(SUBTRACT));
  and ACTIVE_VALID (RESULT_VALID, BOTH_VALID_out, SUBTRACT);

  // Notes on the sheet:
  //   ADD / SUB — gebündelte Operanden- und Validitätsbusse
endmodule
