// Logisim project TinyCPU-Datapath.circ as structural Verilog: 1 circuit, main circuit Datapath
module Datapath (
  input  [15:0] DATA_IN,
  input  ACC_LOAD,
  input  VALID_IN,
  input  CLK,
  output [15:0] ACC_OUT,
  output ACC_VALID_OUT,
  output ZERO,
  output NEGATIVE
);

  wire undriven;

  Register #(.width(16)) ACC (.D(DATA_IN), .Q(ACC_OUT), .clk(undriven));  // open: en, clr
  Register #(.width(1)) ACC_VALID (.D(VALID_IN), .Q(ACC_VALID_OUT), .clk(undriven));  // open: en, clr
  Comparator #(.mode("twosComplement"), .width(16)) ACC_STATUS (
    .a(ACC_OUT), .b({16{1'b0}}), .eq(ZERO), .lt(NEGATIVE));  // open: gt

  // Notes on the sheet:
  //   Clocked 16-bit accumulator; signed comparator derives ZERO and NEGATIVE
endmodule
