// Logisim project TinyCPU-FetchDecode2.circ as structural Verilog: 1 circuit, main circuit FetchDecode
module FetchDecode (
  input  DEC_JUMP_NOT_ZERO,
  input  NOT_ZERO,
  input  ERROR,
  input  DEC_HALT_ERROR,
  output JUMP_NOT_ZERO,
  output HALT_ERROR
);

  // AND_Gate JNZ_TAKEN has open pins: out=JUMP_NOT_ZERO
  // OR_Gate ERROR_HALT has open pins: out=HALT_ERROR

  // Notes on the sheet:
  //   FetchDecode part 2 keeps only processed control signals; direct pass-through pins are omitted.
endmodule
