// Logisim project TinyCPU-Memory.circ as structural Verilog: 1 circuit, main circuit Memory
module Memory (
  input  [11:0] ADDRESS,
  input  WRITE_ENABLE,
  input  VALID_IN,
  input  CLK,
  input  [15:0] DATA_IN,
  output VALID_OUT,
  output [15:0] DATA_OUT
);

  wire undriven, undriven_2;

  RAM #(.addrWidth(12), .dataWidth(16)) DATA_RAM (
    .addr(ADDRESS), .we(WRITE_ENABLE), .oe(1'b1), .clk(CLK), .din(DATA_IN), .dout(DATA_OUT));
  RAM #(.addrWidth(12), .dataWidth(1)) VALID_RAM (
    .we(VALID_IN), .oe(undriven), .clk(undriven_2), .dout(VALID_OUT));  // open: addr, din

  // Notes on the sheet:
  //   4096-word value/valid memory with shared address, write-enable, and clock
endmodule
